# Fritzing sketch portcullis (saved by Fritzing 1.0.3b)
circuit board: 2.99999cm x 11cm
breadboards: 2

parts:
  Att = Rotary Potentiometer (Small) [maximum_resistance=100kΩ knob_status=50% power=0.5W package=THT]
  Rel = Rotary Potentiometer (Small) [maximum_resistance=0.1MΩ knob_status=50% power=0.5W package=THT]
  100K = Resistor [tolerance=±5% resistance=100k power=0.25W package=THT]
  IN1 = PJ-301M [part_number=PJ-301M]
  103 = Ceramic Capacitor [capacitance=10nF voltage=16V package="200 mil [THT, multilayer]"]
  104 = Ceramic Capacitor [capacitance=100nF voltage=16V package="200 mil [THT, multilayer]"]
  J3 = shrouded pin header, 16 pins [form="♂ (shrouded male)"]
  4001 = Diode [package=diode-1n4148]
  Out1 = PJ-301M [part_number=PJ-301M]
  CV1 = PJ-301M [part_number=PJ-301M]
  G1 = PJ-301M [part_number=PJ-301M]
  Out2 = PJ-301M [part_number=PJ-301M]
  IN2 = PJ-301M [part_number=PJ-301M]
  G2 = PJ-301M [part_number=PJ-301M]
  TL074 = TL074 Quad Opamp (Movable) [package="DIP (Dual Inline)"]
  TL074_PWR = TL074 Quad Opamp (Movable) [package="DIP (Dual Inline)"]  # not connected
  TL074_A = TL074 Quad Opamp (Movable) [package="DIP (Dual Inline)"]  # not connected
  TL074_B = TL074 Quad Opamp (Movable) [package="DIP (Dual Inline)"]  # not connected
  TL074_C = TL074 Quad Opamp (Movable) [package="DIP (Dual Inline)"]  # not connected
  TL074_D = TL074 Quad Opamp (Movable) [package="DIP (Dual Inline)"]  # not connected
  Rel_2 = Rotary Potentiometer (Small) [maximum_resistance=100kΩ knob_status=50% power=0.5W package=THT]
  Att_2 = Rotary Potentiometer (Small) [maximum_resistance=100kΩ knob_status=50% power=0.5W package=THT]
  Vactrol1 = VTL5C1
  CV2 = PJ-301M [part_number=PJ-301M]
  Vactrol2 = VTL5C1
  J4 = female pin header, 1 pin [form="♀ (female)"]
  100uF = Electrolytic Capacitor [capacitance=0.1mF voltage=35V package="100 mil [THT, electrolytic]"]
  4_7k = Resistor [tolerance=±5% power=0.25W resistance=4.7k package=THT]
  106 = Ceramic Capacitor [capacitance=10µF voltage=16V package="200 mil [THT, multilayer]"]
  4148 = Diode [package=diode-1n4148]
  4148_2 = Diode [package=diode-1n4148]
  4148_3 = Diode [package=diode-1n4148]
  4148_4 = Diode [package=diode-1n4148]
  4148_5 = Diode [package=diode-1n4148]
  4148_6 = Diode [package=diode-1n4148]
  100K1 = Resistor [tolerance=±5% resistance=100k power=0.25W package=THT]
  106_2 = Ceramic Capacitor [capacitance=10µF voltage=16V package="200 mil [THT, multilayer]"]
  4_7k_2 = Resistor [tolerance=±5% power=0.25W resistance=4.7k package=THT]
  4148_7 = Diode [package=diode-1n4148]
  4148_8 = Diode [package=diode-1n4148]

nets:
  N1: Att.leg1, 4148_2.A
  N2: Att.wiper, Att.leg2, Rel.wiper, Rel.leg2, TL074.connector9, 106.1
  N3: Rel.leg1, 4148_3.A
  N4: 100K.Pin_0, TL074.connector11, 4148.C
  GND: 100K.Pin_1, IN1.Pin_1, 103.0, 104.1, J3.pin2, J3.pin3, J3.pin4, J3.pin13, J3.pin14, J3.pin15, Out1.Pin_1, CV1.Pin_1, G1.Pin_1, Out2.Pin_1, IN2.Pin_1, G2.Pin_1, TL074.connector10, CV2.Pin_1, 100uF.-, 4_7k.Pin_1, 106.0, 100K1.Pin_0, 106_2.1, 4_7k_2.Pin_1
  N5: IN1.Pin_2, CV1.Pin_2, 4148_4.C
  N6: IN1.Pin_3, Vactrol1.Pin_4
  N7: 103.1, 104.0, 4001.C, TL074.connector3, J4.pin1, 100uF.+
  N8: J3.pin1, J3.pin16
  9V: J3.pin5, J3.pin6, J3.pin11, J3.pin12, 4001.A
  N9: J3.pin7, J3.pin10
  N10: J3.pin8, J3.pin9
  N11: Out1.Pin_3, Vactrol1.Pin_3
  N12: CV1.Pin_3, Vactrol1.Pin_2
  N13: G1.Pin_3, 4148.A
  N14: Out2.Pin_3, Vactrol2.Pin_4
  N15: IN2.Pin_2, CV2.Pin_2, 4148_7.C
  N16: IN2.Pin_3, Vactrol2.Pin_3
  N17: G2.Pin_3, 4148_8.A
  N18: TL074.connector0, TL074.connector1, 4148_5.C, 4148_6.C
  N19: TL074.connector2, 100K1.Pin_1, 4148_8.C
  N20: TL074.connector4, Rel_2.wiper, Rel_2.leg2, Att_2.wiper, Att_2.leg2, 106_2.0
  N21: TL074.connector5, TL074.connector6, 4148_7.A
  N22: TL074.connector7, TL074.connector8, 4148_4.A
  N23: TL074.connector12, TL074.connector13, 4148_2.C, 4148_3.C
  N24: Rel_2.leg1, 4148_6.A
  N25: Att_2.leg1, 4148_5.A
  N26: Vactrol1.Pin_1, 4_7k.Pin_0
  N27: CV2.Pin_3, Vactrol2.Pin_2
  N28: Vactrol2.Pin_1, 4_7k_2.Pin_0

notes:
  portcullis
  blueprint@poetaster . de 2025
  jlcjlcjlcjlcjlc

custom parts:
  PJ-301M: Phone power jack.
  TL074 Quad Opamp (Movable): Quadruple Operational Amplifier (Opamp)
  TL074 Quad Opamp (Movable): Quadruple Operational Amplifier (Opamp)
  TL074 Quad Opamp (Movable): Quadruple Operational Amplifier (Opamp)
  TL074 Quad Opamp (Movable): Quadruple Operational Amplifier (Opamp)
  TL074 Quad Opamp (Movable): Quadruple Operational Amplifier (Opamp)
  TL074 Quad Opamp (Movable): Quadruple Operational Amplifier (Opamp)
  VTL5C1: Xvive5C1-R OPTO-ISOLATOR SPECICATION.
